// Logisim project 16bitalu.circ as structural Verilog: 1 circuit, main circuit main
module main (
  input  [15:0] DR,
  input  [15:0] AC,
  input  [7:0] INPR,
  input  E,
  input  [2:0] CG,
  output [15:0] out_6,
  output out_7
);

  wire adder_1_cout;
  wire [15:0] adder_1_out, and_1_out, not_1_out;

  assign and_1_out = DR & AC;  // AND_Gate and_1, 16 bits wide
  assign not_1_out = ~AC;  // NOT_Gate not_1, 16 bits wide
  Adder #(.width(16)) adder_1 (.a(DR), .b(AC), .out(adder_1_out), .cout(adder_1_cout));  // open: cin
  Multiplexer #(.select(3), .width(16)) multiplexer_1 (
    .in0(and_1_out), .in1(adder_1_out), .in2(DR), .in3({{8{1'b0}}, INPR}), .in4(not_1_out),
    .in5({E, AC[15:1]}), .in6({AC[14:0], E}), .out(out_6), .sel(CG));  // open: in7, en
  Multiplexer #(.select(3)) multiplexer_2 (
    .in1(adder_1_cout), .in5(AC[0]), .in6(AC[15]), .out(out_7), .sel(CG));  // open: in0, in2, in3, in4, in7, en

  // Other names for the same wires on the sheet: cu[2:0] = CG
endmodule
