// Logisim project CU.circ as structural Verilog: 1 circuit, main circuit main
module main (
  input  [7:0] T,
  input  [7:0] D,
  input  [11:0] B,
  input  R,
  input  I,
  input  E,
  input  FGI,
  input  FGO,
  input  IEN,
  input  [15:0] DR,
  input  [15:0] AC,
  output MEM_STR,
  output AR_LD,
  output AR_INR,
  output AR_CLR,
  output PC_LD,
  output PC_INR,
  output PC_CLR,
  output DR_LD,
  output DR_INR,
  output [2:0] ALU,
  output AC_LD,
  output AC_INR,
  output AC_CLR,
  output IR_LD,
  output TR_LD,
  output [2:0] S,
  output R_RST,
  output R_1,
  output IEN_RST,
  output IEN_1,
  output E_RST,
  output nE,
  output FGI_RST,
  output FGO_RST,
  output SC_RST,
  output END,
  output OUT
);

  wire and_1_out, or_1_out;

  and and_1 (and_1_out, D[7], I, T[3]);
  and and_2 (OUT, B[10], and_1_out);
  or or_1 (or_1_out, FGI, FGO);
  CU_MEM_main MEM (.T1(T[1]), .T4(T[4]), .T6(T[6]), .D3(D[3]), .D5(D[5]), .D6(D[6]), .R(R), .STR(MEM_STR));
  CU_AR_main AR (
    .T0(T[0]), .T2(T[2]), .T3(T[3]), .T4(T[4]), .R(R), .D5(D[5]), .D7(D[7]), .I(I), .LD(AR_LD), .INR(AR_INR),
    .CLR(AR_CLR));
  CU_PC_main PC (
    .T1(T[1]), .T2(T[2]), .T3(T[3]), .T4(T[4]), .T5(T[5]), .T6(T[6]), .D4(D[4]), .D5(D[5]), .D6(D[6]),
    .D7(D[7]), .B1(B[1]), .B2(B[2]), .B3(B[3]), .B4(B[4]), .B8(B[8]), .B9(B[9]), .R(R), .I(I), .E(E),
    .FGI(FGI), .FGO(FGO), .DR(DR), .AC(AC), .LD(PC_LD), .INR(PC_INR), .CLR(PC_CLR));
  CU_DR_main u_DR (.T4(T[4]), .T5(T[5]), .D0(D[0]), .D1(D[1]), .D2(D[2]), .D6(D[6]), .LD(DR_LD), .INR(DR_INR));
  CU_AC_main u_AC (
    .T3(T[3]), .T5(T[5]), .D0(D[0]), .D1(D[1]), .D2(D[2]), .D7(D[7]), .B5(B[5]), .B6(B[6]), .B7(B[7]),
    .B9(B[9]), .B11(B[11]), .P(and_1_out), .I(I), .ALU(ALU), .LD(AC_LD), .INR(AC_INR), .CLR(AC_CLR));
  CU_IR_main IR (.T1(T[1]), .R(R), .LD(IR_LD));
  CU_TR_main TR (.T0(T[0]), .R(R), .LD(TR_LD));
  CU_BUS_main BUS (
    .T0(T[0]), .T1(T[1]), .T2(T[2]), .T3(T[3]), .T4(T[4]), .T5(T[5]), .T6(T[6]), .D0(D[0]), .D1(D[1]),
    .D2(D[2]), .D3(D[3]), .D4(D[4]), .D5(D[5]), .D6(D[6]), .D7(D[7]), .R(R), .I(I), .P(and_1_out),
    .B10(B[10]), .S(S));
  CU_REG_main F__F (
    .T2(T[2]), .T3(T[3]), .T4(T[4]), .T5(T[5]), .T6(T[6]), .T7(T[7]), .D0(D[0]), .D1(D[1]), .D2(D[2]),
    .D3(D[3]), .D4(D[4]), .D5(D[5]), .D6(D[6]), .D7(D[7]), .B0(B[0]), .B6(B[6]), .B7(B[7]), .B8(B[8]),
    .B10(B[10]), .B11(B[11]), .R(R), .I(I), .R_RST(R_RST), .IEN_RST(IEN_RST), .IEN_1(IEN_1), .E_RST(E_RST),
    .nE(nE), .FGI_RST(FGI_RST), .FGO_RST(FGO_RST), .SC_RST(SC_RST), .END(END));
  and and_3 (R_1, ~T[0], ~T[1], ~T[2], IEN, or_1_out);  // AND_Gate
endmodule
