// Logisim project CU_AC.circ as structural Verilog: 1 circuit, main circuit main
module main (
  input  T3,
  input  T5,
  input  D0,
  input  D1,
  input  D2,
  input  D7,
  input  B5,
  input  B6,
  input  B7,
  input  B9,
  input  B11,
  input  P,
  input  I,
  output [2:0] ALU,
  output LD,
  output INR,
  output CLR
);

  wire and_1_out, and_2_out, and_3_out, and_4_out, and_5_out, and_6_out, and_7_out, and_8_out, not_1_out;

  not not_1 (not_1_out, I);
  and and_1 (and_1_out, D7, not_1_out, T3);
  and and_2 (and_2_out, D0, T5);
  and and_3 (and_3_out, T5, D1);
  and and_4 (and_4_out, T5, D2);
  and and_5 (and_5_out, P, B11);
  and and_6 (and_6_out, and_1_out, B9);
  and and_7 (and_7_out, and_1_out, B7);
  and and_8 (and_8_out, and_1_out, B6);
  and and_9 (INR, and_1_out, B5);
  and and_10 (CLR, and_1_out, B11);
  or or_1 (LD, and_2_out, and_3_out, and_4_out, and_5_out, and_6_out, and_7_out, and_8_out);
  Priority_Encoder priority_encoder_1 (
    .in0(and_2_out), .in1(and_3_out), .in2(and_4_out), .in3(and_5_out), .in4(and_6_out), .in5(and_7_out),
    .in6(and_8_out), .out(ALU));  // open: in7, en_in, gs, en_out
endmodule
