// Logisim project CU_AR.circ as structural Verilog: 1 circuit, main circuit main
module main (
  input  T0,
  input  T2,
  input  T3,
  input  T4,
  input  R,
  input  D5,
  input  D7,
  input  I,
  output LD,
  output INR,
  output CLR
);

  wire and_1_out, and_2_out, and_5_out, not_1_out, not_2_out;

  not not_1 (not_1_out, R);
  not not_2 (not_2_out, D7);
  and and_1 (and_1_out, not_1_out, T0);
  and and_2 (and_2_out, not_1_out, T2);
  and and_3 (INR, D5, T4);
  and and_4 (CLR, R, T0);
  and and_5 (and_5_out, not_2_out, I, T3);
  or or_1 (LD, and_1_out, and_2_out, and_5_out);
endmodule
