// Logisim project CU_BUS.circ as structural Verilog: 1 circuit, main circuit main
module main (
  input  T0,
  input  T1,
  input  T2,
  input  T3,
  input  T4,
  input  T5,
  input  T6,
  input  D0,
  input  D1,
  input  D2,
  input  D3,
  input  D4,
  input  D5,
  input  D6,
  input  D7,
  input  R,
  input  I,
  input  P,
  input  B10,
  output [2:0] S
);

  wire and_1_out, and_2_out, and_3_out, and_4_out, and_5_out, and_6_out, and_7_out, and_8_out, and_9_out,
       and_10_out, and_11_out, and_12_out, and_13_out, and_14_out, not_1_out, not_2_out, not_3_out,
       not_4_out, or_1_out, or_2_out, or_3_out, or_4_out, or_5_out, or_6_out;

  not not_1 (not_1_out, R);
  not not_2 (not_2_out, R);
  and and_1 (and_1_out, D4, T4);
  and and_2 (and_2_out, D5, T5);
  and and_3 (and_3_out, T0, not_1_out);
  and and_4 (and_4_out, T0, R);
  and and_5 (and_5_out, T4, D5);
  and and_6 (and_6_out, T5, D2);
  and and_7 (and_7_out, T6, D6);
  and and_8 (and_8_out, T4, D3);
  and and_9 (and_9_out, T2, not_2_out);
  and and_10 (and_10_out, R, T1);
  not not_3 (not_3_out, R);
  and and_11 (and_11_out, not_3_out, T1);
  not not_4 (not_4_out, D7);
  and and_12 (and_12_out, not_4_out, I, T3);
  or or_1 (or_1_out, D0, D1, D2, D6);
  and and_13 (and_13_out, P, B10);
  or or_2 (or_2_out, and_1_out, and_2_out);
  or or_3 (or_3_out, and_3_out, and_4_out, and_5_out);
  or or_4 (or_4_out, and_6_out, and_7_out);
  or or_5 (or_5_out, and_8_out, and_13_out);
  and and_14 (and_14_out, or_1_out, T4);
  or or_6 (or_6_out, and_11_out, and_12_out, and_14_out);
  Priority_Encoder priority_encoder_1 (
    .in1(or_2_out), .in2(or_3_out), .in3(or_4_out), .in4(or_5_out), .in5(and_9_out), .in6(and_10_out),
    .in7(or_6_out), .out(S));  // open: in0, en_in, gs, en_out
endmodule
