// Logisim project CU_DR.circ as structural Verilog: 1 circuit, main circuit main
module main (
  input  T4,
  input  T5,
  input  D0,
  input  D1,
  input  D2,
  input  D6,
  output LD,
  output INR
);

  wire and_1_out, and_2_out, and_3_out, and_4_out;

  and and_1 (and_1_out, T4, D0);
  buf and_2 (and_2_out, D1);  // AND_Gate
  buf and_3 (and_3_out, D2);  // AND_Gate
  and and_4 (and_4_out, T4, D6);
  and and_5 (INR, D6, T5);
  or or_1 (LD, and_2_out, and_3_out, and_4_out, and_1_out);
endmodule
