// Logisim project CU_IR.circ as structural Verilog: 1 circuit, main circuit main
module main (
  input  T1,
  input  R,
  output LD
);

  wire not_1_out;

  not not_1 (not_1_out, R);
  and and_1 (LD, not_1_out, T1);
endmodule
