// Logisim project CU_MEM.circ as structural Verilog: 1 circuit, main circuit main
module main (
  input  T1,
  input  T4,
  input  T6,
  input  D3,
  input  D5,
  input  D6,
  input  R,
  output STR
);

  wire and_1_out, and_2_out, and_3_out, and_4_out;

  and and_1 (and_1_out, T1, R);
  and and_2 (and_2_out, D3, T4);
  and and_3 (and_3_out, T4, D5);
  and and_4 (and_4_out, T6, D6);
  or or_1 (STR, and_1_out, and_2_out, and_3_out, and_4_out);
endmodule
