// Logisim project CU_PC.circ as structural Verilog: 1 circuit, main circuit main
module main (
  input  T1,
  input  T2,
  input  T3,
  input  T4,
  input  T5,
  input  T6,
  input  D4,
  input  D5,
  input  D6,
  input  D7,
  input  B1,
  input  B2,
  input  B3,
  input  B4,
  input  B8,
  input  B9,
  input  R,
  input  I,
  input  E,
  input  FGI,
  input  FGO,
  input  [15:0] DR,
  input  [15:0] AC,
  output LD,
  output INR,
  output CLR
);

  wire and_1_out, and_2_out, and_3_out, and_4_out, and_5_out, and_6_out, and_7_out, and_8_out, and_10_out,
       and_11_out, and_12_out, and_13_out, and_14_out, nor_1_out, nor_2_out, not_1_out, not_2_out, not_3_out,
       not_4_out;

  not not_1 (not_1_out, I);
  not not_2 (not_2_out, R);
  and and_1 (and_1_out, D7, I, T3);
  and and_2 (and_2_out, D7, not_1_out, T3);
  and and_3 (and_3_out, D4, T4);
  and and_4 (and_4_out, D5, T5);
  and and_5 (and_5_out, not_2_out, T1);
  and and_6 (and_6_out, R, T2);
  and and_7 (and_7_out, B9, FGI, and_1_out);
  and and_8 (and_8_out, B8, FGO, and_1_out);
  not not_3 (not_3_out, AC[15]);
  and and_9 (CLR, R, T1);
  not not_4 (not_4_out, E);
  or or_1 (LD, and_3_out, and_4_out);
  nor nor_1 (nor_1_out, DR[0], DR[1], DR[2], DR[3], DR[4], DR[5], DR[6], DR[7], DR[9], DR[10], DR[11], DR[12], DR[13], DR[14], DR[15], DR[8]);
  and and_10 (and_10_out, and_2_out, not_3_out, B4);
  and and_11 (and_11_out, AC[15], and_2_out, B3);
  and and_12 (and_12_out, and_2_out, B1, not_4_out);
  nor nor_2 (nor_2_out, AC[0], AC[1], AC[2], AC[3], AC[4], AC[5], AC[6], AC[7], AC[9], AC[10], AC[11], AC[12], AC[13], AC[14], AC[15], AC[8]);
  and and_13 (and_13_out, D6, T6, nor_1_out);
  and and_14 (and_14_out, and_2_out, B2, nor_2_out);
  or or_2 (INR, and_5_out, and_6_out, and_13_out, and_7_out, and_8_out, and_10_out, and_11_out, and_12_out, and_14_out);
endmodule
