// Logisim project CU_REG.circ as structural Verilog: 1 circuit, main circuit main
module main (
  input  T2,
  input  T3,
  input  T4,
  input  T5,
  input  T6,
  input  T7,
  input  D0,
  input  D1,
  input  D2,
  input  D3,
  input  D4,
  input  D5,
  input  D6,
  input  D7,
  input  B0,
  input  B6,
  input  B7,
  input  B8,
  input  B10,
  input  B11,
  input  R,
  input  I,
  output R_RST,
  output IEN_RST,
  output IEN_1,
  output E_RST,
  output nE,
  output FGI_RST,
  output FGO_RST,
  output SC_RST,
  output END
);

  wire and_1_out, and_2_out, and_4_out, and_5_out, and_6_out, and_7_out, and_8_out, and_9_out, and_10_out,
       and_11_out, and_12_out, and_13_out, and_18_out, not_1_out;

  and and_1 (and_1_out, D7, I, T3);
  not not_1 (not_1_out, I);
  and and_2 (and_2_out, D7, not_1_out, T3);
  and and_3 (R_RST, R, T2);
  and and_4 (and_4_out, D0, T6);
  and and_5 (and_5_out, D1, T6);
  and and_6 (and_6_out, D2, T6);
  and and_7 (and_7_out, D3, T5);
  and and_8 (and_8_out, D4, T5);
  and and_9 (and_9_out, D5, T6);
  and and_10 (and_10_out, D6, T7);
  and and_11 (and_11_out, D7, not_1_out, T4);
  and and_12 (and_12_out, D7, T4);
  and and_13 (and_13_out, and_1_out, B6);
  and and_14 (E_RST, and_2_out, B10);
  and and_15 (FGO_RST, B10, and_1_out);
  and and_16 (FGI_RST, and_1_out, B11);
  and and_17 (IEN_1, and_1_out, B7);
  and and_18 (and_18_out, R, T3);
  and and_19 (nE, and_2_out, B8);
  and and_20 (END, and_2_out, B0);
  or or_1 (IEN_RST, R_RST, and_13_out);
  or or_2 (SC_RST, and_18_out, and_4_out, and_5_out, and_6_out, and_7_out, and_8_out, and_9_out, and_10_out, and_11_out, and_12_out);
endmodule
