// Logisim project bus_sys.circ as structural Verilog: 1 circuit, main circuit main
module main (
);

  wire ALU_out_7, CLK_out, COMP_RST_q, controlled_buffer_1_out, CU_ac_clr, CU_ac_inr, CU_ac_ld, CU_ar_clr,
       CU_ar_inr, CU_ar_ld, CU_dr_inr, CU_dr_ld, CU_e_rst, CU_end, CU_fgi_rst, CU_fgo_rst, CU_ien_1,
       CU_ien_rst, CU_ir_ld, CU_mem_str, CU_ne, CU_out, CU_pc_clr, CU_pc_inr, CU_pc_ld, CU_r_1, CU_r_rst,
       CU_sc_rst, CU_tr_ld, E_q, E_qn, FGI_q, FGO_q, IEN_q, or_1_out, or_2_out, or_3_out, or_4_out, or_5_out,
       or_6_out, R_q;
  wire [2:0] CU_alu, IR, s;
  wire [3:0] SC_q;
  wire [7:0] decoder_1_out0, INPR_q, T;
  wire [11:0] AR_q, IR_q, PC_q;
  wire [15:0] AC_q, ALU_out_6, bus, DR_q, ram_1_data, TR_q;
  wire [15:15] IR_q_2;

  Register INPR (.Q(INPR_q));  // open: D, en, clk, clr
  D_Flip_Flop COMP_RST (.clk(CLK_out), .Q(COMP_RST_q), .preset(CU_end));  // open: D, Qn, en, reset
  Clock CLK (.out(CLK_out));
  _16bitalu_main ALU (.DR(DR_q), .AC(AC_q), .INPR(INPR_q), .E(E_q), .CG(CU_alu), .out_6(ALU_out_6), .out_7(ALU_out_7));
  or or_1 (or_1_out, controlled_buffer_1_out, ALU_out_7);
  or or_2 (or_2_out, CU_ar_clr, COMP_RST_q);
  or or_3 (or_3_out, CU_pc_clr, COMP_RST_q);
  D_Flip_Flop E (.clk(CLK_out), .D(or_1_out), .Q(E_q), .Qn(E_qn), .reset(or_5_out));  // open: preset, en
  Counter #(.width(12), .max('hfff)) AR (
    .load(CU_ar_ld), .D(bus[11:0]), .count(CU_ar_inr), .Q(AR_q), .clk(CLK_out), .clr(or_2_out));  // open: carry
  Counter #(.width(12), .max('hfff)) PC (
    .load(CU_pc_ld), .D(bus[11:0]), .count(CU_pc_inr), .Q(PC_q), .clk(CLK_out), .clr(or_3_out));  // open: carry
  Counter #(.width(16), .max('hffff)) DR (
    .load(CU_dr_ld), .D(bus), .count(CU_dr_inr), .Q(DR_q), .clk(CLK_out), .clr(COMP_RST_q));  // open: carry
  Counter #(.width(16), .max('hffff)) AC (
    .load(CU_ac_ld), .D(ALU_out_6), .count(CU_ac_inr), .Q(AC_q), .clk(CLK_out), .clr(or_4_out));  // open: carry
  or or_4 (or_4_out, CU_ac_clr, COMP_RST_q);
  or or_5 (or_5_out, CU_e_rst, COMP_RST_q);
  Register #(.width(16)) u_IR (.D(bus), .en(CU_ir_ld), .Q({IR_q_2[15], IR, IR_q}), .clk(CLK_out), .clr(COMP_RST_q));
  Counter #(.width(16), .max('hffff)) TR (
    .load(CU_tr_ld), .D(bus), .count(1'b0), .Q(TR_q), .clk(CLK_out), .clr(COMP_RST_q));  // open: carry
  Register OUTR (.D(bus[7:0]), .en(CU_out), .clk(CLK_out), .clr(COMP_RST_q));  // open: Q
  assign controlled_buffer_1_out = CU_ne ? E_qn : 1'bz;  // Controlled_Buffer controlled_buffer_1
  RAM #(.addrWidth(12), .dataWidth(16), .bus("separate")) ram_1 (
    .addr(AR_q), .din(bus), .data(ram_1_data), .str(CU_mem_str), .clk(CLK_out), .ld(1'b1));  // open: sel, clr
  Multiplexer #(.select(3), .width(16), .enable("false")) multiplexer_1 (
    .in0({16{1'b0}}), .in1({4'b0000, AR_q}), .in2({4'b0000, PC_q}), .in3(DR_q), .in4(AC_q),
    .in5({IR_q_2[15], IR, IR_q}), .in6(TR_q), .in7(ram_1_data), .out(bus), .sel(s));
  D_Flip_Flop IEN (.clk(CLK_out), .Q(IEN_q), .preset(CU_ien_1), .reset(CU_ien_rst));  // open: D, Qn, en
  D_Flip_Flop FGI (.clk(CLK_out), .D(1'b1), .Q(FGI_q), .reset(CU_fgi_rst));  // open: Qn, preset, en
  D_Flip_Flop R (.clk(CLK_out), .D(CU_r_1), .Q(R_q), .reset(CU_r_rst));  // open: Qn, preset, en
  D_Flip_Flop FGO (.clk(CLK_out), .D(1'b1), .Q(FGO_q), .reset(CU_fgo_rst));  // open: Qn, preset, en
  CU_main CU (
    .T(T), .D(decoder_1_out0), .B(IR_q), .R(R_q), .I(IR_q_2[15]), .E(E_q), .FGI(FGI_q), .FGO(FGO_q),
    .IEN(IEN_q), .DR(DR_q), .AC(AC_q), .MEM_STR(CU_mem_str), .AR_LD(CU_ar_ld), .AR_INR(CU_ar_inr),
    .AR_CLR(CU_ar_clr), .PC_LD(CU_pc_ld), .PC_INR(CU_pc_inr), .PC_CLR(CU_pc_clr), .DR_LD(CU_dr_ld),
    .DR_INR(CU_dr_inr), .ALU(CU_alu), .AC_LD(CU_ac_ld), .AC_INR(CU_ac_inr), .AC_CLR(CU_ac_clr),
    .IR_LD(CU_ir_ld), .TR_LD(CU_tr_ld), .S(s), .R_RST(CU_r_rst), .R_1(CU_r_1), .IEN_RST(CU_ien_rst),
    .IEN_1(CU_ien_1), .E_RST(CU_e_rst), .nE(CU_ne), .FGI_RST(CU_fgi_rst), .FGO_RST(CU_fgo_rst),
    .SC_RST(CU_sc_rst), .END(CU_end), .OUT(CU_out));
  Decoder #(.select(3), .enable("false")) decoder_1 (
    .out0(decoder_1_out0[0]), .out1(decoder_1_out0[1]), .out2(decoder_1_out0[2]), .out3(decoder_1_out0[3]),
    .out4(decoder_1_out0[4]), .out5(decoder_1_out0[5]), .out6(decoder_1_out0[6]), .out7(decoder_1_out0[7]),
    .sel(IR));
  Decoder #(.select(4), .enable("false")) decoder_2 (
    .out0(T[0]), .out1(T[1]), .out2(T[2]), .out3(T[3]), .out4(T[4]), .out5(T[5]), .out6(T[6]), .out7(T[7]),
    .sel(SC_q));  // open: out8, out9, out10, out11, out12, out13, out14, out15
  Counter #(.width(4), .max('hf)) SC (.count(1'b1), .Q(SC_q), .clk(CLK_out), .clr(or_6_out));  // open: load, D, carry
  or or_6 (or_6_out, CU_sc_rst, COMP_RST_q);
endmodule
